# Fritzing sketch stackduino-2-smd (saved by Fritzing 0.8.3b)
breadboards: 6

parts:
  Power_plug2 = Power plug
  Btn_3 = Pushbutton 12mm omron
  Encoder1 = Rotary Encoder with Knob
  Btn_4 = Pushbutton [package="[THT]"]
  Btn_5 = Pushbutton [package="[THT]"]
  X1 = USB Connectors [package=usb-microb]
  C10 = Ceramic Capacitor [capacitance=100nF package="0805 [SMD, multilayer]"]
  C11 = Ceramic Capacitor [capacitance=100nF package="0805 [SMD, multilayer]"]
  U2 = ATmega328 [package=tqfp]
  XTAL1 = Crystal [frequency="16 Mhz" package=SMD]
  IC1 = USB to UART Bridge - FT232RL [chip_label=IC package=SSOP28DB]
  L1 = Inductors [package=cdrh2d09]
  LTC1 = LTC4412 [package=ThinSOT]
  IC2 = ILD213T [package=so08]
  MC34063A1 = MC34063A [package=so08]
  DB1 = DB15_rt_female
  A1 = Allegro A3967 [part_number=" A3967" chip_label=" A3967" package=SOIC-24]
  J1 = Dig-ole 128 x 64 0.96" OLED Display [form="♀ (female)" package=THT]
  Power_plug3 = Power plug
  R4 = Resistor [tolerance=±5% resistance=220 package=THT]
  C12 = Electrolytic Capacitor [capacitance=1µF package="100 mil [THT, electrolytic]"]
  C13 = Electrolytic Capacitor [capacitance=1µF package="100 mil [THT, electrolytic]"]
  R5 = Resistor [tolerance=±5% resistance=220 package=THT]
  D1 = Rectifier Diode [part_number=1N4001 package="300 mil [THT]"]
  C14 = Ceramic Capacitor [capacitance=100nF package="100 mil [THT, multilayer]"]
  D2 = Rectifier Diode [part_number=1N4001 package="300 mil [THT]"]
  Q1 = PNP-Transistor [package="TO92 [THT]"]
  R6 = Resistor [tolerance=±5% resistance=220 package=THT]
  C15 = Ceramic Capacitor [capacitance=100nF package="100 mil [THT, multilayer]"]
  C16 = Ceramic Capacitor [capacitance=100nF package="100 mil [THT, multilayer]"]
  C17 = Ceramic Capacitor [capacitance=100nF package="100 mil [THT, multilayer]"]
  C18 = Ceramic Capacitor [capacitance=100nF package="100 mil [THT, multilayer]"]
  C19 = Ceramic Capacitor [capacitance=100nF package="100 mil [THT, multilayer]"]
  C20 = Ceramic Capacitor [capacitance=100nF package="100 mil [THT, multilayer]"]
  R7 = Resistor [tolerance=±5% resistance=220 package=THT]
  C21 = Ceramic Capacitor [capacitance=100nF package="100 mil [THT, multilayer]"]
  J2 = double row female pin header, 6 pins [form="♀ (female)"]
  C22 = Electrolytic Capacitor [capacitance=1µF package="100 mil [THT, electrolytic]"]
  R9 = Resistor [tolerance=±5% resistance=220 package=THT]
  R10 = Resistor [tolerance=±5% resistance=220 package=THT]
  R11 = Resistor [tolerance=±5% resistance=220 package=THT]
  R12 = Resistor [tolerance=±5% resistance=220 package=THT]
  R13 = Resistor [tolerance=±5% resistance=220 package=THT]
  R14 = Resistor [tolerance=±5% resistance=220 package=THT]
  C23 = Ceramic Capacitor [capacitance=100nF package="100 mil [THT, multilayer]"]
  R15 = Resistor [tolerance=±5% resistance=220 package=THT]
  C24 = Ceramic Capacitor [capacitance=100nF package="100 mil [THT, multilayer]"]
  MCP2 = MCP23017 Port Expander [chip_label=IC package=SSOP28DB]
  R16 = Resistor [tolerance=±5% resistance=220 package=THT]
  R17 = Resistor [tolerance=±5% resistance=220 package=THT]
  R8 = Trimmer Potentiometer [maximum_resistance=10kΩ package=THT]
  R18 = Resistor [tolerance=±5% resistance=220 package=THT]
  R19 = Resistor [tolerance=±5% resistance=220 package=THT]
  R20 = Resistor [tolerance=±5% resistance=220 package=THT]
  R21 = Resistor [tolerance=±5% resistance=220 package=THT]
  S1 = Toggle Switch [package=THT]

nets:
  N1: Power_plug2.VCC, D2.anode
  N2: Btn_3.Pin_2, U2.PD3(INT1)
  VCC: Btn_3.Pin_3, U2.VCC, U2.AVCC, U2.AREF, L1.2, MC34063A1.5, A1.Pin_3, A1.Pin_14, J1.Vcc, C13.+, R5.Pin_0, R6.Pin_1, C15.1, C16.1, R7.Pin_0, J2.pin2, R11.Pin_1, R13.Pin_0, MCP2.9, MCP2.18, R16.Pin_0, R17.Pin_0, R8.leg2, R20.Pin_0, S1.L1
  N3: Encoder1.no_name_yet#1, U2.PC2(ADC2)
  GND: Encoder1.no_name_yet#2, Encoder1.no_name_yet#5, Btn_4.Pin_3, Btn_4.Pin_4, Btn_5.Pin_3, Btn_5.Pin_4, X1.GND, C10.1, C11.0, U2.GND, U2.AGND, IC1.7, IC1.18, IC1.21, IC1.25, LTC1.2, LTC1.3, IC2.C1, IC2.C2, IC2.CT1, IC2.CT2, MC34063A1.4, DB1.1, DB1.6, DB1.11, A1.Pin_6, A1.Pin_7, A1.Pin_18, A1.Pin_19, J1.Ground, C12.-, C13.-, R5.Pin_1, D1.cathode, C14.0, C15.0, C16.0, C17.0, C18.0, C19.0, C20.0, J2.pin6, R9.Pin_1, R10.Pin_0, R12.Pin_0, R14.Pin_0, C23.0, R15.Pin_1, C24.0, MCP2.10, R21.Pin_0, S1.COM
  N4: Encoder1.no_name_yet#3, U2.PC3(ADC3)
  N5: Encoder1.no_name_yet#4, MCP2.3
  N6: Btn_4.Pin_1, Btn_4.Pin_2, MCP2.8
  N7: Btn_5.Pin_1, Btn_5.Pin_2, MCP2.7
  N8: X1.D+, IC1.15
  N9: X1.D-, IC1.16
  N10: X1.VBUS, IC1.4, IC1.20, C17.1, C19.1, C20.1
  N11: C10.0, U2.PB7(XTAL2_TOSC2), XTAL1.pin_1
  N12: C11.1, U2.PB6(XTAL1_TOSC1), XTAL1.pin_0
  N13: U2.PD4(XCK_T0), A1.Pin_10
  N14: U2.PD5(T1), A1.Pin_11
  N15: U2.PD6(AIN0), A1.Pin_12
  N16: U2.PD7(AIN1), A1.Pin_13
  N17: U2.PB0(ICP), J1.Data
  N18: U2.PB1(OC1A), J1.Clock
  N19: U2.PB2(SS_OC1B), J1.SS
  N20: U2.PB3(MOSI_OC2), J2.pin4
  N21: U2.PB4(MISO), J2.pin1
  N22: U2.PB5(SCK), J2.pin3
  N23: U2.PC4(ADC4_SDA), MCP2.13, R17.Pin_1
  N24: U2.PC5(ADC5_SCL), MCP2.12, R16.Pin_1
  N25: U2.PC6(_RESET), R7.Pin_1, C21.0, J2.pin5
  N26: U2.PD0(RXD), IC1.5
  N27: U2.PD1(TXD), IC1.1
  N28: U2.PD2(INT0), MCP2.19
  N29: IC1.2, C21.1
  N30: IC1.17, C18.1
  N31: L1.1, MC34063A1.2, D1.anode
  N32: LTC1.1, Power_plug3.GND
  N33: LTC1.4, R6.Pin_0, MCP2.4
  N34: LTC1.5, Q1.B
  N35: LTC1.6, MC34063A1.6, A1.Pin_5, A1.Pin_20, R4.Pin_1, C12.+, D2.cathode, C22.+
  N36: IC2.A1, R18.Pin_1
  N37: IC2.A2, R19.Pin_1
  N38: MC34063A1.1, MC34063A1.7, MC34063A1.8, R4.Pin_0
  N39: MC34063A1.3, C14.1
  N40: DB1.12, A1.Pin_16
  N41: DB1.13, A1.Pin_21
  N42: DB1.14, A1.Pin_9
  N43: DB1.15, A1.Pin_4
  N44: A1.Pin_1, R8.wiper
  N45: A1.Pin_2, R15.Pin_0, C24.1
  N46: A1.Pin_8, R11.Pin_0
  N47: A1.Pin_15, R12.Pin_1
  N48: A1.Pin_17, R10.Pin_1
  N49: A1.Pin_22, R13.Pin_1
  N50: A1.Pin_23, R14.Pin_1, C23.1
  N51: A1.Pin_24, R20.Pin_1, R21.Pin_1
  N52: Power_plug3.VCC, Q1.E
  N53: R9.Pin_0, R8.leg1

notes:
  ATMEGA
  Regulated 5v
  Unregulated Vin
  DC Adapter
  Battery
  POWER
  A3967
  FT232RL
  ICSP
  MCP23017
  DB15
  128 x 64 OLED
  Power switch

custom parts:
  Pushbutton 12mm omron: A generic pushbutton. 12mm
  Rotary Encoder with Knob: Rotary Encoder with 1/4" Shaft and Knob
  LTC4412: Low Loss Powerpath Controller
  MC34063A: 1.5 A, Step-Up/Down/Inverting Switching Regulator
  DB15_rt_female: 15 pin, right-angle female VGA connector. Based on DB9 part by Don Roberts.
  Allegro A3967: Allegro A3967 stepper motor driver in SOIC 24 package
